// Logisim project stovepipe.circ as structural Verilog: 2 circuits, main circuit main
module main (
);

  wire and_1_p1, and_1_p2, and_1_p3, and_1_p5, button_1_out, clock_1_out, cpu_1_read, cpu_1_write;
  wire [7:0] cpu_1_daddr, cpu_1_wdata, ram_1_data, register_1_q;

  Button button_1 (.out(button_1_out));
  Clock clock_1 (.out(clock_1_out));
  CPU cpu_1 (
    .Reset(button_1_out), .Read(cpu_1_read), .Write(cpu_1_write), .Wdata(cpu_1_wdata), .Rdata(ram_1_data),
    .Daddr(cpu_1_daddr), .Clock(clock_1_out));  // open: Dready
  // AND_Gate and_1: pin names not known; wires that end beside it: and_1_p1, and_1_p2, and_1_p3, cpu_1_write, and_1_p5
  Comparator comparator_1 (.a(cpu_1_daddr), .b({8{1'b1}}), .gt(and_1_p1), .eq(and_1_p2), .lt(and_1_p3));
  RAM #(.bus("separate")) ram_1 (
    .addr(cpu_1_daddr), .din(cpu_1_wdata), .data(ram_1_data), .str(cpu_1_write), .clk(clock_1_out),
    .ld(cpu_1_read));  // open: sel, clr
  // Probe on register_1_q
  Register register_1 (.D(cpu_1_wdata), .en(and_1_p5), .Q(register_1_q), .clk(clock_1_out), .clr(button_1_out));
endmodule

module CPU (
  input  Reset,
  input  Clock,
  input  Dready,
  input  [7:0] Rdata,
  output Read,
  output Write,
  output [7:0] Wdata,
  output [7:0] Daddr
);

  wire adder_1_cout, and_1_out, and_2_p1, and_2_p2, and_2_p3, and_3_p3, and_4_p3, and_5_p1, and_5_p2,
       and_5_p3, and_6_p3, comparator_1_eq, comparator_2_eq, decoder_1_out1, decoder_1_out2, decoder_1_out3,
       decoder_1_out5, decoder_1_out7, decoder_2_out2, decoder_2_out3, multiplexer_2_out, multiplexer_3_out,
       not_1_out, or_1_out, or_2_out, or_3_p2;
  wire [2:0] IC_q;
  wire [7:0] A_q, adder_1_out, and_7_p6, AR_q, B_q, IR_q, multiplexer_4_out, or_3_p5, PC_q, rom_1_data,
       shifter_1_out, shifter_2_out, xor_1_p2, xor_1_p3, xor_2_p4;

  Multiplexer #(.width(8)) multiplexer_1 (.in0(AR_q), .in1(PC_q), .out(Daddr), .sel(rom_1_data[7]));  // open: en
  Counter #(.width(3), .max('h7)) IC (
    .load(decoder_1_out7), .D(3'b000), .count(not_1_out), .Q(IC_q), .clk(and_3_p3), .clr(Reset));  // open: carry
  not not_1 (not_1_out, decoder_1_out7);
  Register IR (.D(Wdata), .en(decoder_1_out7), .Q(IR_q), .clk(and_3_p3), .clr(Reset));
  buf and_1 (and_1_out, Dready);  // AND_Gate AND_Gate
  or or_1 (or_1_out, Read, Write);
  assign Wdata = Read ? Rdata : 8'bz;  // Controlled_Buffer controlled_buffer_1
  or or_2 (or_2_out, decoder_1_out3, and_2_p2);
  // AND_Gate and_2: pin names not known; wires that end beside it: and_2_p1, and_2_p2, and_2_p3, or_2_out, rom_1_data[7]
  // AND_Gate and_3: pin names not known; wires that end beside it: and_1_out, Clock, and_3_p3
  // AND_Gate and_4: pin names not known; wires that end beside it: or_2_out, rom_1_data[7], and_4_p3
  ROM #(.addrWidth(7)) rom_1 (.addr({IR_q[3:0], IC_q}), .data(rom_1_data));  // open: sel
  Register AR (.D(Wdata), .en(decoder_1_out5), .Q(AR_q), .clk(and_3_p3), .clr(Reset));
  Counter PC (.load(or_2_out), .D(Wdata), .count(and_4_p3), .Q(PC_q), .clk(and_3_p3), .clr(Reset));  // open: carry
  Decoder #(.select(3)) decoder_1 (
    .out1(decoder_1_out1), .out2(decoder_1_out2), .out3(decoder_1_out3), .out4(and_2_p1),
    .out5(decoder_1_out5), .out6(Write), .out7(decoder_1_out7), .sel(rom_1_data[2:0]));  // open: out0, en
  Decoder #(.select(2)) decoder_2 (
    .out1(Read), .out2(decoder_2_out2), .out3(decoder_2_out3), .sel(rom_1_data[4:3]));  // open: out0
  assign Wdata = decoder_2_out3 ? A_q : 8'bz;  // Controlled_Buffer controlled_buffer_2
  Register A (.D(Wdata), .en(decoder_1_out1), .Q(A_q), .clk(and_3_p3), .clr(Reset));
  Register B (.D(Wdata), .en(decoder_1_out2), .Q(B_q), .clk(and_3_p3), .clr(Reset));
  assign Wdata = decoder_2_out2 ? multiplexer_4_out : 8'bz;  // Controlled_Buffer controlled_buffer_3
  // XOR_Gate #(.width(8)) xor_1: pin names not known; wires that end beside it: B_q, xor_1_p2, xor_1_p3
  assign xor_1_p2 = {{7{comparator_1_eq}}, comparator_1_eq};  // Bit_Extender bit_extender_1
  Comparator #(.width(3)) comparator_1 (.a(3'b011), .b(IR_q[6:4]), .eq(comparator_1_eq));  // open: gt, lt
  Comparator comparator_2 (.a(multiplexer_4_out), .b({8{1'b0}}), .eq(comparator_2_eq));  // open: gt, lt
  // AND_Gate and_5: pin names not known; wires that end beside it: and_5_p1, and_5_p2, and_5_p3
  // AND_Gate and_6: pin names not known; wires that end beside it: and_5_p1, and_5_p1, and_6_p3, and_5_p3
  // OR_Gate #(.width(8)) or_3: pin names not known; wires that end beside it: A_q, or_3_p2, A_q, xor_1_p3, or_3_p5
  // AND_Gate #(.width(8)) and_7: pin names not known; wires that end beside it: or_3_p2, A_q, A_q, A_q, xor_1_p3, and_7_p6
  // XOR_Gate #(.width(8)) xor_2: pin names not known; wires that end beside it: xor_1_p3, A_q, xor_1_p3, xor_2_p4
  Adder adder_1 (.a(A_q), .b(xor_1_p3), .out(adder_1_out), .cin(comparator_1_eq), .cout(adder_1_cout));
  Shifter shifter_1 (.in(A_q), .\dist (3'b001), .out(shifter_1_out));
  Shifter #(.shift("lr")) shifter_2 (.in(A_q), .\dist (3'b001), .out(shifter_2_out));
  Multiplexer #(.select(2)) multiplexer_2 (
    .in0(A_q[0]), .in1(A_q[7]), .in2(adder_1_cout), .in3(adder_1_cout), .out(multiplexer_2_out),
    .sel(IR_q[5:4]));  // open: en
  Register #(.width(1)) ZF (.D(comparator_2_eq), .en(decoder_2_out2), .Q(and_5_p1), .clk(and_3_p3), .clr(Reset));
  Multiplexer #(.select(2)) multiplexer_3 (
    .in0(and_5_p3), .in1(and_5_p1), .in2(and_6_p3), .in3(and_5_p2), .out(multiplexer_3_out), .sel(IR_q[5:4]));  // open: en
  Multiplexer #(.select(3), .width(8)) multiplexer_4 (
    .in0(shifter_2_out), .in1(shifter_1_out), .in2(adder_1_out), .in3(adder_1_out), .in4(xor_2_p4),
    .in5(and_7_p6), .in6(or_3_p5), .in7(xor_1_p3), .out(multiplexer_4_out), .sel(IR_q[6:4]));  // open: en
  Register #(.width(1)) CF (.D(multiplexer_2_out), .en(decoder_2_out2), .Q(and_5_p3), .clk(and_3_p3), .clr(Reset));
  xor xor_3 (and_2_p3, multiplexer_3_out, IR_q[6]);

  // Notes on the sheet:
  //   Clock: pull=down
  //   Reset: pull=down
  //   Dready: pull=up
  //   contents of rom_1 (hex, n*v repeats v):
  //   8f 7*0 11 8f 6*0 8a 11 8f 5*0 8d a 11 8f 4*0 8a 10 8f 5*0 8d a 10 8f 4*0 8d 1e 8f 5*0 8b 8f 6*0 8c
  //   8f 6*0 8d 9 11 1e 8f 0 0 0 1b 8f
endmodule
